// Logisim project 16bit Program Counter Test.circ as structural Verilog: 1 circuit, main circuit main
module main (
);

  wire switch_1_p2, switch_2_p2, switch_3_p2, switch_4_p2;
  wire [15:0] n16bit_pc_1_address;

  // Switch switch_1: pin names not known; wires that end beside it: 1'b1, switch_1_p2
  // Switch switch_2: pin names not known; wires that end beside it: 1'b1, switch_2_p2
  // Switch switch_3: pin names not known; wires that end beside it: 1'b1, switch_3_p2
  // Switch switch_4: pin names not known; wires that end beside it: 1'b1, switch_4_p2
  Pull_Resistor pull_resistor_1 (.node(switch_1_p2));
  Pull_Resistor pull_resistor_2 (.node(switch_2_p2));
  Pull_Resistor pull_resistor_3 (.node(switch_3_p2));
  Pull_Resistor pull_resistor_4 (.node(switch_4_p2));
  _16bit_PC u_16bit_pc_1 (
    .Address(n16bit_pc_1_address), .Index_Write({8{1'b0}}), .Branch({8{1'b0}}),
    .Index_Write_Signal(switch_1_p2), .Branch_Signal(switch_2_p2), .Write_Address(switch_3_p2),
    .Count(switch_4_p2));
  LED led_1 (.in(n16bit_pc_1_address[7]));
  LED led_2 (.in(n16bit_pc_1_address[15]));
  LED led_3 (.in(n16bit_pc_1_address[5]));
  LED led_4 (.in(n16bit_pc_1_address[6]));
  LED led_5 (.in(n16bit_pc_1_address[13]));
  LED led_6 (.in(n16bit_pc_1_address[14]));
  LED led_7 (.in(n16bit_pc_1_address[4]));
  LED led_8 (.in(n16bit_pc_1_address[3]));
  LED led_9 (.in(n16bit_pc_1_address[12]));
  LED led_10 (.in(n16bit_pc_1_address[11]));
  LED led_11 (.in(n16bit_pc_1_address[0]));
  LED led_12 (.in(n16bit_pc_1_address[2]));
  LED led_13 (.in(n16bit_pc_1_address[1]));
  LED led_14 (.in(n16bit_pc_1_address[9]));
  LED led_15 (.in(n16bit_pc_1_address[10]));
  LED led_16 (.in(n16bit_pc_1_address[8]));

  // Notes on the sheet:
  //   Index Address
  //   Branch Address
endmodule
