// Logisim project 16bit Program Counter.circ as structural Verilog: 1 circuit, main circuit 16bit PC
// PC - 16
module _16bit_PC (
  input  [7:0] Index_Write,
  input  [7:0] Branch,
  input  Index_Write_Signal,
  input  Branch_Signal,
  input  Write_Address,
  input  Count,
  output [15:0] Address
);

  wire undriven;
  wire [7:0] adder_1_out, controlled_buffer_2_out, Program_Counter_q_out;

  Controlled_Buffer #(.width(8), .negatecontrol("true")) controlled_buffer_1 (
    .in(Branch), .en(Branch_Signal));  // open: out
  assign controlled_buffer_2_out = ~Index_Write_Signal ? Index_Write : 8'bz;  // Controlled_Buffer controlled_buffer_2
  _8bit_Register Index_Register (
    .Data(controlled_buffer_2_out), .Write_Signal(Index_Write_Signal), .Read_Signal(Write_Address),
    .Q_Out(Address[7:0]));  // open: Clock
  _8bit_Register Program_Counter (
    .Data(adder_1_out), .Write_Signal(Write_Address), .Read_Signal(Count), .Q_Out(Program_Counter_q_out));  // open: Clock
  _8bit_Register MAR_2 (
    .Data(Program_Counter_q_out), .Write_Signal(Count), .Read_Signal(Write_Address), .Q_Out(Address[15:8]));  // open: Clock
  Adder adder_1 (.a(Address[15:8]), .b(8'h1), .out(adder_1_out), .cin(undriven));  // open: cout
  Pull_Resistor pull_resistor_1 (.node(Address));

  // Notes on the sheet:
  //   Address: pull=down
  //   Write_Address: pull=down
  //   Count: pull=down
  //   Index_Write_Signal: pull=down
  //   Index_Write: pull=down
  //   Branch: pull=down
  //   Branch_Signal: pull=down
endmodule
