// Logisim project 4bit Jimin ALU.circ as structural Verilog: 1 circuit, main circuit 4bit ALU
// ALU
module _4bit_ALU (
  input  [3:0] Operand_A,
  input  [3:0] Operand_B,
  input  [2:0] Operation,
  output [3:0] ALU_OUT
);

  wire [3:0] _4bit_AND_out, _4bit_NOT_out, _4bit_OR_out, _4bit_XOR_out, adder_1_out, demultiplexer_1_out0,
       demultiplexer_1_out1, demultiplexer_1_out2, demultiplexer_1_out3, demultiplexer_1_out4,
       demultiplexer_1_out5, demultiplexer_2_out0, demultiplexer_2_out1, demultiplexer_2_out2,
       demultiplexer_2_out3, demultiplexer_2_out4, subtractor_1_out;

  Demultiplexer #(.select(3), .width(4), .enable("false")) demultiplexer_1 (
    .out0(demultiplexer_1_out0), .out1(demultiplexer_1_out1), .out2(demultiplexer_1_out2),
    .out3(demultiplexer_1_out3), .out4(demultiplexer_1_out4), .out5(demultiplexer_1_out5), .in(Operand_A),
    .sel(Operation));  // open: out6, out7
  Demultiplexer #(.select(3), .width(4), .enable("false")) demultiplexer_2 (
    .out0(demultiplexer_2_out0), .out1(demultiplexer_2_out1), .out2(demultiplexer_2_out2),
    .out3(demultiplexer_2_out3), .out4(demultiplexer_2_out4), .in(Operand_B), .sel(Operation));  // open: out5, out6, out7
  Adder #(.width(4)) adder_1 (
    .a(demultiplexer_1_out0), .b(demultiplexer_2_out0), .out(adder_1_out));  // open: cin, cout
  Subtractor #(.width(4)) subtractor_1 (
    .a(demultiplexer_1_out1), .b(demultiplexer_2_out1), .out(subtractor_1_out));  // open: bin, bout
  assign _4bit_OR_out = demultiplexer_1_out2 | demultiplexer_2_out2;  // OR_Gate _4bit_OR, 4 bits wide
  assign _4bit_AND_out = demultiplexer_1_out3 & demultiplexer_2_out3;  // AND_Gate _4bit_AND, 4 bits wide
  assign _4bit_XOR_out = demultiplexer_1_out4 ^ demultiplexer_2_out4;  // XOR_Gate _4bit_XOR, 4 bits wide
  assign _4bit_NOT_out = ~demultiplexer_1_out5;  // NOT_Gate _4bit_NOT, 4 bits wide
  Multiplexer #(.select(3), .width(4), .enable("false")) multiplexer_1 (
    .in0(adder_1_out), .in1(subtractor_1_out), .in2(_4bit_OR_out), .in3(_4bit_AND_out), .in4(_4bit_XOR_out),
    .in5(_4bit_NOT_out), .out(ALU_OUT), .sel(Operation));  // open: in6, in7

  // Notes on the sheet:
  //   Operand A
  //   Operand B
endmodule
