// Logisim project 74HC574 8bit DFF.circ as structural Verilog: 1 circuit, main circuit 8bit D FF
// 74HC574
module _8bit_D_FF (
  input  [7:0] Data,
  input  Clock,
  output [7:0] OutPut
);

  Register #(.Select("low")) register_1 (
    .D(Data), .en(1'b1), .Q(OutPut), .clk(Clock), .clr(1'b0), .cs(1'b0), .preset(1'b0));

  // Notes on the sheet:
  //   Clock: pull=down
  //   OutPut: pull=down
  //   Data: pull=down
endmodule
