// Logisim project 8bit PC Test.circ as structural Verilog: 1 circuit, main circuit main
module main (
  output [7:0] out_1,
  output [7:0] out_2
);

  wire pull_resistor_1_node, pull_resistor_2_node, pull_resistor_4_node, s_r_ff_1_q, switch_2_p2,
       switch_3_p2, switch_4_p2, switch_6_p2;
  wire [7:0] Program_Counter_q_out;

  Pull_Resistor pull_resistor_1 (.node(pull_resistor_1_node));
  // Switch switch_1: pin names not known; wires that end beside it: 1'b1, pull_resistor_1_node, pull_resistor_1_node
  // Switch switch_2: pin names not known; wires that end beside it: 1'b1, switch_2_p2
  // Switch switch_3: pin names not known; wires that end beside it: 1'b1, switch_3_p2
  // Switch switch_4: pin names not known; wires that end beside it: 1'b1, switch_4_p2
  Pull_Resistor pull_resistor_2 (.node(pull_resistor_2_node));
  // Switch switch_5: pin names not known; wires that end beside it: 1'b1, pull_resistor_2_node
  // Switch switch_6: pin names not known; wires that end beside it: 1'b1, switch_6_p2
  Pull_Resistor pull_resistor_3 (.node(switch_6_p2));
  Pull_Resistor pull_resistor_4 (.node(pull_resistor_4_node));
  // Switch switch_7: pin names not known; wires that end beside it: 1'b1, pull_resistor_4_node
  S_R_Flip_Flop s_r_ff_1 (
    .S(switch_6_p2), .clk(pull_resistor_2_node), .R(pull_resistor_4_node), .Q(s_r_ff_1_q));  // open: Qn, preset, reset
  _8bit_Register Program_Counter (
    .Data(out_1), .Write_Signal(pull_resistor_1_node), .Read_Signal(switch_2_p2),
    .Q_Out(Program_Counter_q_out));  // open: Clock
  _8bit_Register MAR (
    .Data(Program_Counter_q_out), .Write_Signal(switch_3_p2), .Read_Signal(switch_4_p2), .Q_Out(out_2));  // open: Clock
  Adder adder_1 (.a(out_2), .b(8'h1), .out(out_1));  // open: cin, cout
  LED led_1 (.in(s_r_ff_1_q));
  LED led_2 (.in(Program_Counter_q_out[0]));
  LED led_3 (.in(Program_Counter_q_out[1]));
  LED led_4 (.in(Program_Counter_q_out[2]));
  LED led_5 (.in(Program_Counter_q_out[3]));
  LED led_6 (.in(Program_Counter_q_out[4]));
  LED led_7 (.in(Program_Counter_q_out[5]));
  LED led_8 (.in(Program_Counter_q_out[6]));
  LED led_9 (.in(Program_Counter_q_out[7]));

  // Notes on the sheet:
  //   out_1: pull=down
  //   out_2: pull=down
  //   Write
  //   Read
  //   Write
  //   Read
endmodule
