// Logisim project 8bit Reg Test.circ as structural Verilog: 1 circuit, main circuit main
module main (
);

  wire controlled_buffer_2_out, pull_resistor_1_node, pull_resistor_2_node, switch_2_p2;
  wire [7:0] controlled_buffer_1_out, switch_1_p3;

  Pull_Resistor pull_resistor_1 (.node(pull_resistor_1_node));
  assign controlled_buffer_1_out = pull_resistor_1_node ? 8'h5 : 8'bz;  // Controlled_Buffer controlled_buffer_1
  // Switch switch_1: pin names not known; wires that end beside it: 1'b1, pull_resistor_1_node, switch_1_p3
  // Switch switch_2: pin names not known; wires that end beside it: 1'b1, switch_2_p2
  assign controlled_buffer_2_out = pull_resistor_2_node ? 1'b1 : 1'bz;  // Controlled_Buffer controlled_buffer_2
  Pull_Resistor pull_resistor_2 (.node(pull_resistor_2_node));
  // Switch switch_3: pin names not known; wires that end beside it: 1'b1, pull_resistor_2_node
  LED led_1 (.in(controlled_buffer_2_out));
  _8bit_SR_Register u_8bit_sr_register_1 (
    .Data(controlled_buffer_1_out), .Write(pull_resistor_1_node), .Read(switch_2_p2), .Out(switch_1_p3));
  LED led_2 (.in(switch_1_p3[0]));
  LED led_3 (.in(switch_1_p3[1]));
  LED led_4 (.in(switch_1_p3[2]));
  LED led_5 (.in(switch_1_p3[3]));
  LED led_6 (.in(switch_1_p3[4]));
  LED led_7 (.in(switch_1_p3[5]));
  LED led_8 (.in(switch_1_p3[6]));
  LED led_9 (.in(switch_1_p3[7]));
endmodule
