// Logisim project 8bit Register Test.circ as structural Verilog: 1 circuit, main circuit main
module main (
  input  [7:0] in_1,
  output [7:0] out_2,
  output [7:0] out_3
);

  wire clock_1_out, switch_1_p2, switch_2_p3, switch_3_p2, switch_4_p3;

  Clock clock_1 (.out(clock_1_out));
  // Switch switch_1: pin names not known; wires that end beside it: 1'b1, switch_1_p2
  Pull_Resistor pull_resistor_1 (.node(switch_1_p2));
  // Switch switch_2: pin names not known; wires that end beside it: 1'b1, 1'b1, switch_2_p3
  Pull_Resistor pull_resistor_2 (.node(switch_2_p3));
  // Switch switch_3: pin names not known; wires that end beside it: 1'b1, switch_3_p2
  // Switch switch_4: pin names not known; wires that end beside it: 1'b1, 1'b1, switch_4_p3
  _8bit_Register u_8bit_register_1 (
    .Data(in_1), .Write_Signal(switch_1_p2), .Read_Signal(switch_2_p3), .Q_Out(out_2), .Clock(clock_1_out));
  Pull_Resistor pull_resistor_3 (.node(out_2));
  Pull_Resistor pull_resistor_4 (.node(switch_3_p2));
  Pull_Resistor pull_resistor_5 (.node(switch_4_p3));
  _8bit_Register u_8bit_register_2 (
    .Data(out_2), .Write_Signal(switch_3_p2), .Read_Signal(switch_4_p3), .Q_Out(out_3), .Clock(clock_1_out));
  Pull_Resistor pull_resistor_6 (.node(out_3));

  // Notes on the sheet:
  //   out_3: pull=down
  //   out_2: pull=down
  //   in_1: pull=down
endmodule
