// Logisim project 8bit Register.circ as structural Verilog: 1 circuit, main circuit 8bit Register
// 8bit Reg
module _8bit_Register (
  input  [7:0] Data,
  input  Write_Signal,
  input  Read_Signal,
  input  Clock,
  output [7:0] Q_Out
);

  wire and_2_out, pull_resistor_1_node;
  wire [7:0] d_ff_7_q;

  Pull_Resistor pull_resistor_1 (.node(pull_resistor_1_node));
  and and_1 (pull_resistor_1_node, Write_Signal, Clock);
  D_Flip_Flop d_ff_1 (.clk(pull_resistor_1_node), .D(Data[3]), .Q(d_ff_7_q[3]));  // open: Qn, preset, reset
  D_Flip_Flop d_ff_2 (.clk(pull_resistor_1_node), .D(Data[7]), .Q(d_ff_7_q[7]));  // open: Qn, preset, reset
  and and_2 (and_2_out, Read_Signal, Clock);
  D_Flip_Flop d_ff_3 (.clk(pull_resistor_1_node), .D(Data[2]), .Q(d_ff_7_q[2]));  // open: Qn, preset, reset
  D_Flip_Flop d_ff_4 (.clk(pull_resistor_1_node), .D(Data[6]), .Q(d_ff_7_q[6]));  // open: Qn, preset, reset
  D_Flip_Flop d_ff_5 (.clk(pull_resistor_1_node), .D(Data[1]), .Q(d_ff_7_q[1]));  // open: Qn, preset, reset
  D_Flip_Flop d_ff_6 (.clk(pull_resistor_1_node), .D(Data[5]), .Q(d_ff_7_q[5]));  // open: Qn, preset, reset
  D_Flip_Flop d_ff_7 (.clk(pull_resistor_1_node), .D(Data[0]), .Q(d_ff_7_q[0]));  // open: Qn, preset, reset
  D_Flip_Flop d_ff_8 (.clk(pull_resistor_1_node), .D(Data[4]), .Q(d_ff_7_q[4]));  // open: Qn, preset, reset
  assign Q_Out = and_2_out ? d_ff_7_q : 8'bz;  // Controlled_Buffer controlled_buffer_1
  Pull_Resistor pull_resistor_2 (.node(Q_Out));
  Pull_Resistor pull_resistor_3 (.node(and_2_out));

  // Notes on the sheet:
  //   Data: pull=down
  //   Clock: pull=down
  //   Write_Signal: pull=down
  //   Q_Out: pull=down
  //   Read_Signal: pull=down
endmodule
