// Logisim project 8bit SR Register.circ as structural Verilog: 1 circuit, main circuit 8bit SR Register
// 8bit REG
module _8bit_SR_Register (
  input  [7:0] Data,
  input  Write,
  input  Read,
  output [7:0] Out
);

  wire [7:0] controlled_buffer_1_out, controlled_inverter_1_out, s_r_ff_7_q;

  Pull_Resistor pull_resistor_1 (.node(Write));
  assign controlled_buffer_1_out = Write ? Data : 8'bz;  // Controlled_Buffer controlled_buffer_1
  assign controlled_inverter_1_out = Write ? ~Data : 8'bz;  // Controlled_Inverter controlled_inverter_1
  Pull_Resistor pull_resistor_2 (.node(controlled_inverter_1_out));
  Pull_Resistor pull_resistor_3 (.node(Write));
  S_R_Flip_Flop s_r_ff_1 (
    .S(controlled_buffer_1_out[3]), .clk(Write), .R(controlled_inverter_1_out[3]), .Q(s_r_ff_7_q[3]));  // open: Qn, preset, reset
  S_R_Flip_Flop s_r_ff_2 (
    .S(controlled_buffer_1_out[7]), .clk(Write), .R(controlled_inverter_1_out[7]), .Q(s_r_ff_7_q[7]));  // open: Qn, preset, reset
  S_R_Flip_Flop s_r_ff_3 (
    .S(controlled_buffer_1_out[2]), .clk(Write), .R(controlled_inverter_1_out[2]), .Q(s_r_ff_7_q[2]));  // open: Qn, preset, reset
  S_R_Flip_Flop s_r_ff_4 (
    .S(controlled_buffer_1_out[6]), .clk(Write), .R(controlled_inverter_1_out[6]), .Q(s_r_ff_7_q[6]));  // open: Qn, preset, reset
  S_R_Flip_Flop s_r_ff_5 (
    .S(controlled_buffer_1_out[1]), .clk(Write), .R(controlled_inverter_1_out[1]), .Q(s_r_ff_7_q[1]));  // open: Qn, preset, reset
  S_R_Flip_Flop s_r_ff_6 (
    .S(controlled_buffer_1_out[5]), .clk(Write), .R(controlled_inverter_1_out[5]), .Q(s_r_ff_7_q[5]));  // open: Qn, preset, reset
  S_R_Flip_Flop s_r_ff_7 (
    .S(controlled_buffer_1_out[0]), .clk(Write), .R(controlled_inverter_1_out[0]), .Q(s_r_ff_7_q[0]));  // open: Qn, preset, reset
  S_R_Flip_Flop s_r_ff_8 (
    .S(controlled_buffer_1_out[4]), .clk(Write), .R(controlled_inverter_1_out[4]), .Q(s_r_ff_7_q[4]));  // open: Qn, preset, reset
  Pull_Resistor pull_resistor_4 (.node(Read));
  assign Out = Read ? s_r_ff_7_q : 8'bz;  // Controlled_Buffer controlled_buffer_2

  // Notes on the sheet:
  //   Out: pull=down
  //   Data: pull=down
  //   Read: pull=down
  //   Write: pull=down
  //   Reset
  //   Set
endmodule
